# Fritzing sketch PCB (saved by Fritzing 0.9.3b)
circuit board: 4.30148cm x 2.44454cm
breadboards: 1

parts:
  TSL2591 = Adafruit TSL2591 [part_number="Adafruit #1980"]
  J1 = female pin header, 4 pins [form="♀ (female)"]
  R1 = Resistor [tolerance=±5% resistance=220 package=THT]  # not connected

nets:
  N1: TSL2591.VIN, J1.pin1
  N2: TSL2591.GND, J1.pin2
  N3: TSL2591.SDA, J1.pin3
  N4: TSL2591.SCL, J1.pin4

notes:
  Husnal
  RVR

custom parts:
  Adafruit TSL2591: When the future is dazzlingly-bright, this ultra-high-range luminosity sensor will help you measure it. The TSL2591 luminosity sensor is an advanced digital light sensor, ideal for use in a wide range of light situations. Compared to low cost CdS cells, this sensor is more precise, allowing for exact lux calculations and can be configured for different gain/timing ranges to detect light ranges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
