# Fritzing sketch PCB2 (saved by Fritzing 0.9.3b)
circuit board: 3.25675cm x 2.63593cm
breadboards: 1

parts:
  J2 = female pin header, 4 pins [form="♀ (female)"]
  TSL2592 = Adafruit TSL2591 [part_number="Adafruit #1980"]

nets:
  N1: J2.pin1, TSL2592.VIN
  N2: J2.pin2, TSL2592.GND
  N3: J2.pin3, TSL2592.SDA
  N4: J2.pin4, TSL2592.SCL

notes:
  Husnal
  RVR
  SCL
  SDA
  GND
  Vin

custom parts:
  Adafruit TSL2591: When the future is dazzlingly-bright, this ultra-high-range luminosity sensor will help you measure it. The TSL2591 luminosity sensor is an advanced digital light sensor, ideal for use in a wide range of light situations. Compared to low cost CdS cells, this sensor is more precise, allowing for exact lux calculations and can be configured for different gain/timing ranges to detect light ranges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
